# Fritzing sketch P1-Blink (saved by Fritzing 0.9.3b)
breadboards: 1

parts:
  Part1 = Arduino Nano (Rev3.0)
  WhiteLEDmodule1 = WhiteLEDmodule
  DigitalPushButtonV1 = DigitalPushButtonV2
  WhiteLEDmodule2 = WhiteLEDmodule
  U1 = POT [package=trim_pot]

nets:
  GND: Part1.GND, WhiteLEDmodule1.GND, DigitalPushButtonV1.GND, WhiteLEDmodule2.GND, U1.A
  N1: Part1.D2, DigitalPushButtonV1.Input
  N2: Part1.D5, WhiteLEDmodule1.INPUT
  N3: Part1.D7, WhiteLEDmodule2.INPUT
  N4: Part1.A0, U1.E
  N5: Part1.3V3, WhiteLEDmodule1.POWER, DigitalPushButtonV1.Signal, WhiteLEDmodule2.POWER, U1.S
